// Logisim project Final_project.circ as structural Verilog
module main (
  input  EN
);

  wire and_1_out, and_2_out, clk, countdown10_1_zero, Cross, cross_button, cross_out, G1, G2, nor_1_out,
       nState, or_1_out, pedestrian_button_1_en, R1, R2, reset_out, Y1, Y2;
  wire [3:0] cross_count, DownCounter_v1_1_count, multiplexer_1_out;
  wire [7:0] HEX0, HEX1;

  and and_1 (and_1_out, ~multiplexer_1_out[0], ~multiplexer_1_out[1], ~multiplexer_1_out[2], ~multiplexer_1_out[3]);  // AND_Gate
  Button reset (.out(reset_out));
  nor nor_1 (nor_1_out, Cross, cross_button);
  and and_2 (and_2_out, EN, and_1_out);
  Clock u_clk (.out(clk));
  // RGBLED LED_R: pin names not known; wires that end beside it: R1
  // RGBLED LED_Y: pin names not known; wires that end beside it: Y1, Y1
  // RGBLED LED_G: pin names not known; wires that end beside it: and_1_out, G1
  or or_1 (or_1_out, nState, pedestrian_button_1_en);
  countdown10 countdown10_1 (.rst(nor_1_out), .en(Cross), .clk(clk), .count(cross_count), .zero(countdown10_1_zero));
  // RGBLED rgbled_1: pin names not known; wires that end beside it: R2
  // RGBLED rgbled_2: pin names not known; wires that end beside it: Y2, Y2
  // RGBLED rgbled_3: pin names not known; wires that end beside it: G2
  FSM3 fsm3_1 (
    .en(EN), .nState(and_2_out), .reset(reset_out), .button(cross_button), .G1(G1), .Y1(Y1), .R1(R1),
    .G2(G2), .Y2(Y2), .R2(R2), .\cross (Cross), .rst(nState));
  _7_Segment_Display #(.active("false")) L_7_Segment_Display_1 (
    .g(HEX1[6]), .f(HEX1[5]), .a(HEX1[0]), .b(HEX1[1]), .e(HEX1[4]), .d(HEX1[3]), .c(HEX1[2]), .dp(HEX1[7]));
  DownCounter_v1 DownCounter_v1_1 (.en(or_1_out), .clk(clk), .count(DownCounter_v1_1_count));
  pedestrian_button pedestrian_button_1 (.counter(DownCounter_v1_1_count), .en(pedestrian_button_1_en));
  LED Cross_Light (.in(Cross));
  _7_Segment_Display #(.active("false")) L_7_Segment_Display_2 (
    .g(HEX0[6]), .f(HEX0[5]), .a(HEX0[0]), .b(HEX0[1]), .e(HEX0[4]), .d(HEX0[3]), .c(HEX0[2]), .dp(HEX0[7]));
  Multiplexer #(.width(4)) multiplexer_1 (
    .in0(DownCounter_v1_1_count), .in1(cross_count), .out(multiplexer_1_out), .sel(Cross));
  Button u_cross (.out(cross_out));
  J_K_Flip_Flop j_k_ff_1 (
    .J(cross_out), .K(countdown10_1_zero), .clk(clk), .Q(cross_button));  // open: Qn, preset, reset
  Bin2Hex Bin2Hex_1 (
    .in3(multiplexer_1_out[3]), .in2(multiplexer_1_out[2]), .in1(multiplexer_1_out[1]),
    .in0(multiplexer_1_out[0]), .Hex1(HEX1), .Hex0(HEX0));

  // Notes on the sheet:
  //   Traffic Light A
  //   Traffic Light B
  //   Counter Display
endmodule

module myComparator (
  input  v3,
  input  v2,
  input  v1,
  output z
);

  wire and_1_out, and_2_out;

  and and_1 (and_1_out, v3, v1);
  and and_2 (and_2_out, v3, v2);
  or or_1 (z, and_1_out, and_2_out);
endmodule

module Seg7_Decoder (
  input  i_m3,
  input  i_m2,
  input  i_m1,
  input  i_m0,
  output [7:0] o_seg
);

  wire and_1_out, and_2_out, and_3_out, and_4_out, and_5_out, and_6_out, and_7_out, and_8_out, and_9_out,
       and_10_out, and_11_out, and_12_out, and_13_out, and_14_out, and_15_out, and_16_out, and_17_out,
       and_18_out, and_19_out, and_20_out, and_21_out, and_22_out, and_23_out, not_1_out, not_2_out,
       not_3_out, not_4_out;

  not not_1 (not_1_out, i_m3);
  not not_2 (not_2_out, i_m2);
  not not_3 (not_3_out, i_m1);
  not not_4 (not_4_out, i_m0);
  and and_1 (and_1_out, not_1_out, not_2_out, not_3_out);
  and and_2 (and_2_out, not_1_out, i_m2, i_m1, i_m0);
  and and_3 (and_3_out, i_m3, not_2_out, i_m1);
  and and_4 (and_4_out, not_1_out, not_2_out, i_m0);
  and and_5 (and_5_out, not_1_out, not_2_out, i_m1);
  and and_6 (and_6_out, not_2_out, i_m1, i_m0);
  and and_7 (and_7_out, i_m3, i_m2, not_3_out);
  and and_8 (and_8_out, not_1_out, i_m2, not_3_out);
  and and_9 (and_9_out, i_m3, i_m2, i_m1);
  and and_10 (and_10_out, not_1_out, not_2_out, not_3_out, i_m0);
  and and_11 (and_11_out, not_1_out, i_m2, not_3_out, not_4_out);
  and and_12 (and_12_out, not_1_out, i_m2, i_m1, i_m0);
  and and_13 (and_13_out, i_m3, not_2_out, i_m1, i_m0);
  and and_14 (and_14_out, i_m3, i_m2, i_m1, not_4_out);
  and and_15 (and_15_out, not_1_out, not_2_out, i_m1, not_4_out);
  and and_16 (and_16_out, i_m3, i_m2, not_3_out, not_4_out);
  and and_17 (and_17_out, not_1_out, i_m2, not_3_out, i_m0);
  and and_18 (and_18_out, not_1_out, i_m2, i_m1, not_4_out);
  and and_19 (and_19_out, i_m3, i_m2, i_m1, i_m0);
  and and_20 (and_20_out, not_1_out, not_2_out, not_3_out, i_m0);
  and and_21 (and_21_out, not_1_out, i_m2, not_3_out, not_4_out);
  and and_22 (and_22_out, i_m3, not_2_out, i_m1, i_m0);
  and and_23 (and_23_out, i_m3, i_m2, i_m1, not_4_out);
  or or_1 (o_seg[6], and_1_out, and_2_out, and_3_out);
  or or_2 (o_seg[5], and_4_out, and_5_out, and_6_out, and_7_out);
  or or_3 (o_seg[4], i_m0, and_8_out, and_9_out);
  or or_4 (o_seg[3], and_10_out, and_11_out, and_12_out, and_13_out, and_14_out);
  or or_5 (o_seg[2], and_15_out, and_16_out);
  or or_6 (o_seg[1], and_17_out, and_18_out, and_19_out);
  or or_7 (o_seg[0], and_20_out, and_21_out, and_22_out, and_23_out);

  assign o_seg[7] = 1'b1;
endmodule

module CircuitB (
  input  z,
  output s6,
  output s5,
  output s4,
  output s3,
  output s2,
  output s1,
  output s0
);


  assign s0 = z;
  assign s1 = 1'b0;
  assign s2 = 1'b0;
  assign s3 = z;
  assign s4 = z;
  assign s5 = z;
  assign s6 = 1'b1;
endmodule

module Bin2Hex (
  input  in3,
  input  in2,
  input  in1,
  input  in0,
  output [7:0] Hex1,
  output [7:0] Hex0
);

  wire z;

  myComparator comparator1 (.v3(in3), .v2(in2), .v1(in1), .z(z));
  CircuitB b1 (.z(z), .s6(Hex1[6]), .s5(Hex1[5]), .s4(Hex1[4]), .s3(Hex1[3]), .s2(Hex1[2]), .s1(Hex1[1]), .s0(Hex1[0]));
  Seg7_Decoder decoder (.i_m3(in3), .i_m2(in2), .i_m1(in1), .i_m0(in0), .o_seg(Hex0));

  assign Hex1[7] = 1'b1;
endmodule

module FSM (
  input  en,
  input  nState,
  input  reset,
  output G1,
  output Y1,
  output R1,
  output G2,
  output Y2,
  output R2,
  output rst
);

  wire and_5_out, and_6_out, not_1_out, not_2_out, not_3_out;
  wire [2:0] multiplexer_1_out, register_1_q;

  Multiplexer #(.select(4), .width(3)) multiplexer_1 (
    .in0(3'b000), .in1(3'b001), .in2(3'b010), .in3(3'b011), .in4(3'b100), .in5(3'b101), .in8(3'b001),
    .in9(3'b010), .in10(3'b011), .in11(3'b100), .in12(3'b101), .in13(3'b000), .out(multiplexer_1_out),
    .sel({en, register_1_q}));  // open: in6, in7, in14, in15
  // Probe on multiplexer_1_out
  Register #(.width(3)) register_1 (.D(multiplexer_1_out), .Q(register_1_q), .clk(nState), .clr(reset));  // open: en
  // Probe on register_1_q
  not not_1 (not_1_out, register_1_q[2]);
  not not_2 (not_2_out, register_1_q[1]);
  not not_3 (not_3_out, register_1_q[0]);
  and and_1 (G1, not_1_out, not_2_out, not_3_out);
  and and_2 (Y1, not_1_out, not_2_out, register_1_q[0]);
  or or_1 (R1, register_1_q[1], register_1_q[2]);
  and and_3 (G2, register_1_q[1], register_1_q[0]);
  and and_4 (Y2, register_1_q[2], not_3_out);
  and and_5 (and_5_out, not_1_out, not_3_out);
  and and_6 (and_6_out, not_2_out, register_1_q[0]);
  or or_2 (R2, and_5_out, and_6_out);

  assign rst = nState;
endmodule

module DownCounter_v1 (
  input  en,
  input  clk,
  output [3:0] count
);

  wire and_1_out, and_2_out, and_3_out, and_4_out, t_ff_1_q, t_ff_2_q, t_ff_3_q;

  T_Flip_Flop t_ff_1 (.T(en), .clk(clk), .Q(t_ff_1_q), .Qn(count[0]));  // open: reset, preset
  and and_1 (and_1_out, count[0], count[1], count[2], count[3]);
  and and_2 (and_2_out, en, t_ff_1_q);
  T_Flip_Flop t_ff_2 (.T(and_2_out), .clk(clk), .Q(t_ff_2_q), .Qn(count[1]));  // open: reset, preset
  and and_3 (and_3_out, and_2_out, t_ff_2_q);
  T_Flip_Flop t_ff_3 (.T(and_3_out), .clk(clk), .Q(t_ff_3_q), .Qn(count[2]), .preset(and_1_out));  // open: reset
  and and_4 (and_4_out, and_3_out, t_ff_3_q);
  T_Flip_Flop t_ff_4 (.T(and_4_out), .clk(clk), .Qn(count[3]), .preset(and_1_out));  // open: Q, reset

  // Notes on the sheet:
  //   Synchronous Down Counter from 3 to 0 with reset
endmodule

module pedestrian_button (
  input  [3:0] counter,
  output en
);

  or or_1 (en, counter[0], counter[1], counter[2], counter[3]);
endmodule

module CircuitA (
  input  i2,
  input  i1,
  input  i0,
  output o2,
  output o1,
  output o0
);

  not not_1 (o1, i1);
  and and_1 (o2, i2, i1);

  assign o0 = i0;
endmodule

module countdown10 (
  input  rst,
  input  en,
  input  clk,
  output [3:0] count,
  output zero
);

  wire and_1_out, or_1_out;

  and and_1 (and_1_out, or_1_out, en);
  T_Flip_Flop t_ff_1 (.T(and_1_out), .clk(clk), .Q(count[0]), .reset(rst));  // open: Qn, preset
  T_Flip_Flop t_ff_2 (.T(and_1_out), .clk(count[0]), .Q(count[1]), .preset(rst));  // open: Qn, reset
  T_Flip_Flop t_ff_3 (.T(and_1_out), .clk(count[1]), .Q(count[2]), .reset(rst));  // open: Qn, preset
  T_Flip_Flop t_ff_4 (.T(and_1_out), .clk(count[2]), .Q(count[3]), .preset(rst));  // open: Qn, reset
  or or_1 (or_1_out, count[0], count[1], count[2], count[3]);
  not not_1 (zero, or_1_out);

  // Other names for the same wires on the sheet: Reset = rst
endmodule

module test (
  input  a,
  input  b,
  input  c,
  output G1,
  output Y1,
  output R1,
  output G2,
  output Y2,
  output R2
);

  wire and_5_out, and_6_out, not_1_out, not_2_out, not_3_out;

  not not_1 (not_1_out, a);
  not not_2 (not_2_out, b);
  not not_3 (not_3_out, c);
  and and_1 (G1, not_1_out, not_2_out, not_3_out);
  and and_2 (Y1, not_1_out, not_2_out, c);
  or or_1 (R1, b, a);
  and and_3 (G2, b, c);
  and and_4 (Y2, a, not_3_out);
  and and_5 (and_5_out, not_1_out, not_3_out);
  or or_2 (R2, and_5_out, and_6_out);
  and and_6 (and_6_out, not_2_out, c);
endmodule

module FSM3 (
  input  en,
  input  nState,
  input  reset,
  input  button,
  output G1,
  output Y1,
  output R1,
  output G2,
  output Y2,
  output R2,
  output \cross ,
  output rst
);

  wire all_red, and_6_out, and_7_out, not_1_out, not_2_out, not_3_out;
  wire [2:0] multiplexer_1_out;
  wire [4:0] and_1_out;

  and and_1 (and_1_out[4], button, all_red);
  Multiplexer #(.select(5), .width(3)) multiplexer_1 (
    .in0(3'b000), .in1(3'b001), .in2(3'b010), .in3(3'b011), .in4(3'b100), .in5(3'b101), .in6(3'b101),
    .in7(3'b101), .in8(3'b001), .in9(3'b010), .in10(3'b011), .in11(3'b100), .in12(3'b101), .in13(3'b000),
    .in14(3'b101), .in15(3'b101), .in16(3'b000), .in17(3'b001), .in18(3'b110), .in19(3'b011), .in20(3'b100),
    .in21(3'b110), .in22(3'b101), .in23(3'b101), .in24(3'b001), .in25(3'b010), .in26(3'b110), .in27(3'b100),
    .in28(3'b110), .in29(3'b110), .in30(3'b101), .in31(3'b101), .out(multiplexer_1_out),
    .sel({and_1_out[4], en, and_1_out[2:0]}));
  // Probe on multiplexer_1_out
  Register #(.width(3)) register_1 (.D(multiplexer_1_out), .Q(and_1_out[2:0]), .clk(nState), .clr(reset));  // open: en
  // Probe on and_1_out[2:0]
  not not_1 (not_1_out, and_1_out[2]);
  not not_2 (not_2_out, and_1_out[1]);
  not not_3 (not_3_out, and_1_out[0]);
  and and_2 (G1, not_1_out, not_2_out, not_3_out);
  and and_3 (Y1, not_1_out, not_2_out, and_1_out[0]);
  or or_1 (R1, and_1_out[1], and_1_out[2]);
  and and_4 (G2, and_1_out[1], and_1_out[0]);
  and and_5 (Y2, and_1_out[2], not_2_out, not_3_out);
  and and_6 (and_6_out, not_1_out, not_3_out);
  and and_7 (and_7_out, not_2_out, and_1_out[0]);
  and and_8 (\cross , not_3_out, and_1_out[1], and_1_out[2]);
  or or_2 (R2, and_6_out, and_7_out, \cross );
  and and_9 (all_red, R1, R2);

  assign rst = nState;
endmodule
