// Logisim project Lab_8.circ as structural Verilog: 1 circuit, main circuit main
module main (
  input  s0,
  input  s1,
  output Output_1,
  output Output_2,
  output Output_3
);

  wire clock_2_out;
  wire [0:0] blink_red;
  wire [1:1] blink_green;
  wire [2:0] counter_1_q;

  Clock #(.highDuration(2), .lowDuration(2)) clock_1 (.out(blink_red[0]));
  Counter #(.max('h7), .width(3)) counter_1 (
    .Q(counter_1_q), .up(1'b0), .clk(clock_2_out));  // open: load, D, count, carry, clr
  Clock clock_2 (.out(clock_2_out));
  Multiplexer #(.select(2), .width(3)) multiplexer_1 (
    .in0(counter_1_q), .in1({2'b00, blink_red[0]}), .in2({1'b0, blink_green[1], 1'b0}), .in3(counter_1_q),
    .out({Output_3, Output_2, Output_1}), .sel({s1, s0}));
  Clock #(.highDuration(4), .lowDuration(4)) clock_3 (.out(blink_green[1]));
endmodule
