// Logisim project mux_decoder_adder.circ as structural Verilog: 3 circuits, main circuit MUX_FULL_ADDER
module main (
  input  C_IN,
  input  A,
  input  B,
  output C_OUT_1,
  output TOTAL_1,
  output C_OUT_2,
  output TOTAL_2
);

  MUX_FULL_ADDER mux_full_adder_1 (.CIN(C_IN), .A(A), .B(B), .C_OUT(C_OUT_1), .TOTAL(TOTAL_1));
  DECODER_FULL_ADDER decoder_full_adder_1 (.A(A), .B(B), .CIN(C_IN), .TOTAL(C_OUT_2), .COUT(TOTAL_2));
endmodule

module MUX_FULL_ADDER (
  input  CIN,
  input  A,
  input  B,
  output C_OUT,
  output TOTAL
);

  Multiplexer #(.select(3)) multiplexer_1 (
    .in0(1'b0), .in1(1'b0), .in2(1'b1), .in3(1'b0), .in4(1'b1), .in5(1'b0), .in6(1'b1), .in7(1'b1),
    .out(TOTAL), .sel({B, A, CIN}));
  Multiplexer #(.select(3)) multiplexer_2 (
    .in0(1'b0), .in1(1'b0), .in2(1'b0), .in3(1'b1), .in4(1'b0), .in5(1'b1), .in6(1'b1), .in7(1'b1),
    .out(C_OUT), .sel({B, A, CIN}));
endmodule

module DECODER_FULL_ADDER (
  input  A,
  input  B,
  input  CIN,
  output TOTAL,
  output COUT
);

  wire decoder_1_out1, decoder_1_out2, decoder_1_out4, decoder_1_out7, decoder_2_out3, decoder_2_out5,
       decoder_2_out6, decoder_2_out7;

  Decoder #(.select(3)) decoder_1 (
    .out1(decoder_1_out1), .out2(decoder_1_out2), .out4(decoder_1_out4), .out7(decoder_1_out7),
    .sel({CIN, B, A}));  // open: out0, out3, out5, out6, en
  Decoder #(.select(3)) decoder_2 (
    .out3(decoder_2_out3), .out5(decoder_2_out5), .out6(decoder_2_out6), .out7(decoder_2_out7),
    .sel({CIN, B, A}));  // open: out0, out1, out2, out4, en
  or or_1 (TOTAL, decoder_1_out1, decoder_1_out2, decoder_1_out4, decoder_1_out7);
  or or_2 (COUT, decoder_2_out3, decoder_2_out5, decoder_2_out6, decoder_2_out7);
endmodule
